# Fritzing sketch steckbrett_usb (saved by Fritzing 1.0.8)
breadboards: 1

parts:
  M1 = Seeed Studio XIAO ESP32S3 Plus (gesteckt)
  M2 = WIZnet WIZ850io (gesteckt)

nets:
  N1: M1.D0, M2.J2-5_RSTn
  N2: M1.D1, M2.J2-6_MISO
  N3: M1.D3, M2.J1-6_INTn
  N4: M1.D8, M2.J1-3_MOSI
  N5: M1.D9, M2.J1-4_SCLK
  N6: M1.D10, M2.J1-5_SCSn
  N7: M1.3V3, M2.J2-2_3V3D, M2.J2-3_3V3D
  N8: M1.GND, M2.J1-1_GND, M2.J1-2_GND, M2.J2-1_GND

custom parts:
  Seeed Studio XIAO ESP32S3 Plus (gesteckt): XIAO ESP32S3 Plus (16 MB Flash, 8 MB PSRAM, U.FL) in zwei Buchsenleisten 1x7. Nur die 14 Randstifte, ohne die SMD-Pads der Rueckseite. Draufsicht, USB-C oben.
  WIZnet WIZ850io (gesteckt): WIZ850io (W5500, RJ45 mit Uebertrager) in zwei Buchsenleisten 1x6, Isolierkoerper 11 mm. Draufsicht, RJ45-Oeffnung oben.
