# Fritzing sketch traegerplatine (saved by Fritzing 1.0.8)
circuit board: 3.3cm x 8.65cm
breadboards: 1

parts:
  J1 = Leiterplattenklemme 2-polig, Raster 5,08 mm
  F1 = PTC-Sicherung 0,5 A / 60 V (z. B. Littelfuse RXEF050)
  D1 = Schottky-Diode 1N5819
  D2 = TVS-Diode P6KE33A
  C1 = Elektrolytkondensator 22µF 50V, Raster 2,54 mm
  U2 = LDO-Regler MCP1702-3302E/TO (3,3 V, 250 mA)
  C4 = Keramikkondensator 1µF 50V, Raster 5,08 mm
  U1 = Traco TSR 1-2450 (5 V)
  M2 = WIZnet WIZ850io (gesteckt)
  C3 = Keramikkondensator 1µF 50V, Raster 5,08 mm
  M1 = Seeed Studio XIAO ESP32S3 Plus (gesteckt)
  D3 = Schottky-Diode 1N5819
  C2 = Elektrolytkondensator 47µF 16V, Raster 2,54 mm

nets:
  P24_ROH: J1.1_+24V, F1.1
  GND: J1.2_GND, D2.anode, C1.-, U2.1_GND, C4.1, U1.2_GND, M2.J1-1_GND, M2.J1-2_GND, M2.J2-1_GND, C3.1, M1.GND, C2.-
  P24_F: F1.2, D1.anode
  VIN: D1.cathode, D2.cathode, C1.+, U1.1_+Vin
  P5V: U2.2_VIN, C4.2, U1.3_+Vout, D3.anode
  P3V3_ETH: U2.3_VOUT, M2.J2-2_3V3D, M2.J2-3_3V3D, C3.2
  MOSI: M2.J1-3_MOSI, M1.D8
  SCLK: M2.J1-4_SCLK, M1.D9
  CS: M2.J1-5_SCSn, M1.D10
  INT: M2.J1-6_INTn, M1.D3
  RST: M2.J2-5_RSTn, M1.D0
  MISO: M2.J2-6_MISO, M1.D1
  P5V_XIAO: M1.5V, D3.cathode, C2.+

notes:
  24V DC

custom parts:
  Leiterplattenklemme 2-polig, Raster 5,08 mm: Schraubklemme 2-polig, Raster 5,08 mm, Bohrung 1,3 mm, Bauhoehe hoechstens 10,5 mm (Schulter des Gehaeuses). Leitereinfuehrung unten.
  PTC-Sicherung 0,5 A / 60 V (z. B. Littelfuse RXEF050): Rueckstellende Sicherung, Haltestrom 0,5 A, >= 60 V, radial, Raster 5,08 mm.
  Schottky-Diode 1N5819: 1N5819 im Gehaeuse DO-41, liegend, Raster 7,62 mm. Ring = Kathode (links).
  TVS-Diode P6KE33A: P6KE33A im Gehaeuse DO-15, liegend, Raster 10,16 mm. Ring = Kathode (links).
  Elektrolytkondensator 22µF 50V, Raster 2,54 mm: Elko radial 22µF 50V, Raster 2,54 mm, Durchmesser bis 6,3 mm. Bauhoehe nach Einbauort (Spec Abschnitt 2.1).
  LDO-Regler MCP1702-3302E/TO (3,3 V, 250 mA): Microchip MCP1702-3302E/TO, Festspannungsregler 3,3 V, 250 mA, Eingang bis 13,2 V, TO-92. Beinchen auf Raster 2,54 aufgebogen. Je 1 uF Keramik an Ein- und Ausgang (Datenblatt Abschnitt 5).
  Keramikkondensator 1µF 50V, Raster 5,08 mm: Vielschicht-Keramikkondensator X7R 1µF 50V, bedrahtet, Raster 5,08 mm, Koerper bis 7,1 x 4,1 x 9,2 mm.
  Traco TSR 1-2450 (5 V): Traco TSR 1-2450, Schaltregler im SIP3-Gehaeuse, 1 A, Ausgang 5 V. Keine Leiterbahnen unter dem Gehaeuse (Datenblatt).
  WIZnet WIZ850io (gesteckt): WIZ850io (W5500, RJ45 mit Uebertrager) in zwei Buchsenleisten 1x6, Isolierkoerper 11 mm. Draufsicht, RJ45-Oeffnung oben.
  Seeed Studio XIAO ESP32S3 Plus (gesteckt): XIAO ESP32S3 Plus (16 MB Flash, 8 MB PSRAM, U.FL) in zwei Buchsenleisten 1x7. Nur die 14 Randstifte, ohne die SMD-Pads der Rueckseite. Draufsicht, USB-C oben.
  Elektrolytkondensator 47µF 16V, Raster 2,54 mm: Elko radial 47µF 16V, Raster 2,54 mm, Durchmesser bis 6,3 mm. Bauhoehe nach Einbauort (Spec Abschnitt 2.1).
